// Logisim project RSC.circ as structural Verilog: 12 circuits, main circuit main
module main (
  input  RESET_PC,
  input  PC30,
  input  NOP_FLUSHING,
  input  NotFlushSEL,
  input  FlushSEL
);

  wire bios_1_p2, bios_1_p3, branch_1_breq, branch_1_brlt, comparator_1_eq, comparator_2_eq, dmem_1_p3,
       imem_1_p2, reg_1_p5, reg_1_p6, uart_read_1_p2;
  wire [1:0] uart_write_1_p3;
  wire [4:0] multiplexer_2_p4_2;
  wire [7:0] multiplexer_3_out, multiplexer_10_out;
  wire [11:0] multiplexer_2_p4_3;
  wire [13:0] adder_1_out, adder_2_out, adder_3_out, adder_4_out, adder_5_out, cycle_counter_q,
       Inst_counter_q, multiplexer_1_out, PC_q, PC_W_q;
  wire [13:1] undriven, undriven_2;
  wire [14:0] multiplexer_2_p4;
  wire [31:0] A_q, alu_1_result, ALU_RESULT_q, B_q, Imm_q, immediate_1_imm, Inst_XM_q, multiplexer_4_out,
       multiplexer_5_out, multiplexer_6_out, multiplexer_7_out, multiplexer_8_out, multiplexer_9_out,
       PC_XM_q, reg_1_p1, reg_1_p2;

  Adder #(.width(14)) adder_1 (.a(14'h4), .b(PC_q), .out(adder_1_out));  // open: cin, cout
  Adder #(.width(14)) adder_2 (.a(PC_q), .b(immediate_1_imm[13:0]), .out(adder_2_out));  // open: cin, cout
  Multiplexer #(.select(2), .width(14)) multiplexer_1 (
    .in0(adder_1_out), .in1(alu_1_result[13:0]), .in2(adder_2_out), .in3({undriven, RESET_PC}),
    .out(multiplexer_1_out));  // open: sel
  Register Inst_counter (.D(adder_4_out[7:0]), .Q(Inst_counter_q[7:0]));  // open: en, clk, clr
  Register cycle_counter (.D(adder_3_out[7:0]), .Q(cycle_counter_q[7:0]));  // open: en, clk, clr
  Register #(.width(14)) PC (.D(multiplexer_1_out), .Q(PC_q));  // open: en, clk, clr
  Adder #(.width(14)) adder_3 (.a(14'h1), .b(cycle_counter_q), .out(adder_3_out));  // open: cin, cout
  Adder #(.width(14)) adder_4 (
    .a({undriven_2, NotFlushSEL}), .b(Inst_counter_q), .out(adder_4_out));  // open: cin, cout
  // IMEM imem_1: pin names not known; wires that end beside it: multiplexer_1_out, imem_1_p2
  // BIOS bios_1: pin names not known; wires that end beside it: multiplexer_1_out, bios_1_p2, bios_1_p3
  // Multiplexer #(.select(2), .width(32)) multiplexer_2: pin names not known; wires that end beside it: imem_1_p2, bios_1_p2, PC30, {multiplexer_2_p4_3, multiplexer_2_p4_2, multiplexer_2_p4}
  // Reg reg_1: pin names not known; wires that end beside it: reg_1_p1, reg_1_p2, multiplexer_2_p4_2, multiplexer_2_p4_3, reg_1_p5, reg_1_p6
  immediate immediate_1 (.Instruc({multiplexer_2_p4_3, multiplexer_2_p4_2, multiplexer_2_p4}), .Imm(immediate_1_imm));
  Register PC_XM (.D(PC_q[7:0]), .Q(PC_XM_q[7:0]));  // open: en, clk, clr
  Register A (.D(multiplexer_3_out), .Q(A_q[7:0]));  // open: en, clk, clr
  Multiplexer multiplexer_3 (.in0(reg_1_p5), .in1(reg_1_p1[0]), .out(multiplexer_3_out[0]));  // open: sel
  Register #(.width(32)) B (.D(multiplexer_4_out), .Q(B_q));  // open: en, clk, clr
  Multiplexer multiplexer_4 (.in0(reg_1_p6), .in1(reg_1_p1[0]), .out(multiplexer_4_out[0]));  // open: sel
  Register #(.width(32)) Imm (.D(immediate_1_imm), .Q(Imm_q));  // open: en, clk, clr
  Register #(.width(32)) Inst_XM (
    .D({multiplexer_2_p4_3, multiplexer_2_p4_2, multiplexer_2_p4}), .Q(Inst_XM_q));  // open: en, clk, clr
  Multiplexer #(.width(32)) multiplexer_5 (.in0(A_q), .in1(reg_1_p1), .out(multiplexer_5_out));  // open: sel
  Multiplexer #(.width(32)) multiplexer_6 (.in0(B_q), .in1(reg_1_p1), .out(multiplexer_6_out));  // open: sel
  Multiplexer multiplexer_7 (.in0(Inst_XM_q[0]), .in1(NOP_FLUSHING), .out(multiplexer_7_out[0]), .sel(FlushSEL));
  Multiplexer #(.select(2), .width(32)) multiplexer_8 (
    .in0(multiplexer_5_out), .in1(PC_XM_q), .out(multiplexer_8_out));  // open: in2, in3, sel
  Multiplexer #(.select(2), .width(32)) multiplexer_9 (
    .in0(multiplexer_6_out), .in1(Imm_q), .out(multiplexer_9_out));  // open: in2, in3, sel
  Branch branch_1 (
    .A(multiplexer_5_out), .B(multiplexer_6_out), .BrEq(branch_1_breq), .BrLT(branch_1_brlt));  // open: BrUn
  ALU alu_1 (.A(multiplexer_8_out), .B(multiplexer_9_out), .result(alu_1_result));  // open: ALUSel
  Multiplexer multiplexer_10 (.in0(alu_1_result[0]), .out(multiplexer_10_out[0]));  // open: in1, sel
  Comparator comparator_1 (.a(multiplexer_10_out), .b(8'h4), .eq(comparator_1_eq));  // open: gt, lt
  Comparator comparator_2 (.a(multiplexer_10_out), .b(8'h8), .eq(comparator_2_eq));  // open: gt, lt
  // Controls controls_1: pin names not known; wires that end beside it: branch_1_breq, branch_1_brlt, {multiplexer_2_p4_3, multiplexer_2_p4_2, multiplexer_2_p4}, multiplexer_7_out, reg_1_p2
  Register PC_W (.D(PC_XM_q[7:0]), .Q(PC_W_q[7:0]));  // open: en, clk, clr
  Register #(.width(32)) ALU_RESULT (.D(alu_1_result), .Q(ALU_RESULT_q));  // open: en, clk, clr
  Register #(.width(32)) Inst_W (.D(multiplexer_7_out), .Q(reg_1_p2));  // open: en, clk, clr
  // DMEM dmem_1: pin names not known; wires that end beside it: multiplexer_10_out, multiplexer_6_out, dmem_1_p3
  // UART_read uart_read_1: pin names not known; wires that end beside it: comparator_1_eq, uart_read_1_p2, uart_write_1_p3[1]
  // UART_write uart_write_1: pin names not known; wires that end beside it: multiplexer_6_out, comparator_2_eq, uart_write_1_p3[0]
  Adder #(.width(14)) adder_5 (.a(14'h4), .b(PC_W_q), .out(adder_5_out));  // open: cin, cout
  Multiplexer #(.select(3)) multiplexer_11 (
    .in0(dmem_1_p3), .in1(ALU_RESULT_q[0]), .in2(adder_5_out[0]), .in3(uart_read_1_p2),
    .in4(uart_write_1_p3[0]), .out(reg_1_p1[0]));  // open: in5, in6, in7, sel
  // Pins of 8 and 32 bits meet at 32'h80000008
  // Pins of 8 and 32 bits meet at 32'h80000004
  // Pins of 1 and 32 bits meet at {{30{1'b0}}, uart_write_1_p3}
  // Pins of 1 and 14 bits meet at {undriven, RESET_PC}
  // Pins of 1 and 14 bits meet at {undriven_2, NotFlushSEL}
  // Pins of 1 and 32 bits meet at reg_1_p1
  // Pins of 1 and 8 bits meet at multiplexer_3_out
  // Pins of 1 and 32 bits meet at multiplexer_4_out
  // Pins of 1 and 32 bits meet at Inst_XM_q
  // Pins of 1 and 32 bits meet at multiplexer_7_out
  // Pins of 8 and 32 bits meet at A_q
  // Pins of 8 and 32 bits meet at PC_XM_q

  // Notes on the sheet:
  //   alu
  //   jal & branch predict taken
  //   pc+4
endmodule

module IMEM (
  input  A_din,
  input  A_addr,
  input  A_wbe,
  input  B_din,
  input  B_addr,
  input  B_wbe,
  input  clk,
  output [31:0] A_dout,
  output [31:0] B_dout
);
endmodule

module Reg (
  input  DataD,
  input  AddrD,
  input  AddrA,
  input  AddrB,
  input  clk,
  output [31:0] DataA,
  output [31:0] DataB
);
endmodule

module DMEM (
  input  [13:0] addr,
  input  [31:0] din,
  input  wbe,
  input  clk,
  output [31:0] dout
);
endmodule

module ALU (
  input  [31:0] A,
  input  [31:0] B,
  input  ALUSel,
  output [31:0] result
);
endmodule

module Branch (
  input  [31:0] A,
  input  [31:0] B,
  input  BrUn,
  output BrEq,
  output BrLT
);
endmodule

module immediate (
  input  [31:0] Instruc,
  output [31:0] Imm
);
endmodule

module Forwarding (
  input  Inst_FD,
  input  Inst_XM,
  input  Inst_W
);
endmodule

module Controls (
  input  BrEq,
  input  BrLT,
  input  Inst_FD,
  input  Inst_XM,
  input  Inst_W,
  output PCSel,
  output RegWEn,
  output ImmSel,
  output BrUn,
  output Bsel,
  output ASel,
  output ALUSel,
  output MemRW,
  output WBSel
);
endmodule

module BIOS (
  input  A_din,
  input  A_addr,
  input  A_wbe,
  input  B_din,
  input  B_addr,
  input  B_wbe,
  input  clk,
  output [31:0] A_dout,
  output [31:0] B_dout
);
endmodule

module UART_read (
  input  ready_recieve,
  output [13:0] read,
  output [31:0] read_valid
);
endmodule

module UART_write (
  input  [13:0] write,
  input  [31:0] write_valid,
  output ready_to_write
);
endmodule
